# Fritzing sketch chargerController (saved by Fritzing 0.9.3b)
perfboards: 10
breadboards: 1

parts:
  R12 = Resistor [tolerance=±5% resistance=15k package=THT]
  R13 = Resistor [tolerance=±5% resistance=2.2k package=THT]
  R14 = Resistor [tolerance=±5% resistance=6.8k package=THT]
  R15 = Resistor [tolerance=±5% resistance=47k package=THT]
  C5 = Ceramic Capacitor [capacitance=0.47mF voltage=50V package="100 mil [THT, multilayer]"]
  C6 = Ceramic Capacitor [capacitance=0.47mF voltage=50V package="100 mil [THT, multilayer]"]
  C7 = Ceramic Capacitor [capacitance=0.47mF voltage=50V package="100 mil [THT, multilayer]"]
  C8 = Ceramic Capacitor [capacitance=0.47mF voltage=50V package="100 mil [THT, multilayer]"]  # not connected
  R16 = Photocell (LDR) [package=THT]
  R17 = Resistor [tolerance=±5% resistance=220 package=THT]  # not connected
  R18 = Resistor [tolerance=±5% resistance=220 package=THT]
  R19 = Resistor [tolerance=±5% resistance=220 package=THT]  # not connected
  R20 = Resistor [tolerance=±5% resistance=220 package=THT]  # not connected
  R21 = Resistor [tolerance=±5% resistance=220 package=THT]  # not connected
  R22 = Resistor [tolerance=±5% resistance=220 package=THT]
  U8 = Voltage Regulator - Variable [package="TO220 [THT]"]  # not connected
  U9 = Voltage Regulator - Variable [package="TO220 [THT]"]  # not connected
  U10 = Voltage Regulator - Variable [package="TO220 [THT]"]  # not connected
  U11 = LM 358 Dual Op-Amp [package="SO 08 [SMD]"]
  U12 = LM 358 Dual Op-Amp [package="SO 08 [SMD]"]  # not connected
  U13 = LM 358 Dual Op-Amp [package="SO 08 [SMD]"]
  Q4 = MOSFET-NCHANNEL [package=to220v]  # not connected
  Q5 = MOSFET-NCHANNEL [package=to220v]  # not connected
  Q6 = MOSFET-NCHANNEL [package=to220v]  # not connected
  LCD2 = LCD screen
  Componente3 = Arduino Nano (Rev3.0)
  U14 = Voltage Regulator - 5V [package="TO220 [THT]"]
  Componente4 = Real Time Clock Module - DS1307 RTC Breakout Board
  U15 = MCP23017 [package=dil28-3]
  KEYPAD1 = Membrane Matrix Keypad
  R23 = Resistor [tolerance=±5% resistance=10k package=THT]

nets:
  N1: R12.Pin_0, R13.Pin_0
  N2: R14.Pin_0, C7.0, Componente3.A3
  N3: R14.Pin_1, U14.input_voltage
  VDD: R15.Pin_0, LCD2.VDD, Componente3.VIN, U14.output_voltage, Componente4.5V, U15.VCC
  N4: R15.Pin_1, R16.pin_0
  GND: C5.1, C6.1, C7.1, R16.pin_1, LCD2.VSS, LCD2.R/W, Componente3.GND, Componente4.GND, U15.GND
  N5: R18.Pin_1, U13.connector3
  N6: R22.Pin_1, U11.connector3
  N7: LCD2.RS, Componente3.D12/MISO
  N8: LCD2.E, Componente3.D11/MOSI
  N9: LCD2.DB4, Componente3.D8
  N10: LCD2.DB5, Componente3.D7
  N11: LCD2.DB6, Componente3.D6
  N12: LCD2.DB7, Componente3.D5
  N13: Componente3.D2, Componente4.SQW
  N14: Componente3.D3, Componente4.SCL
  N15: Componente3.D4, Componente4.SDA
  N16: Componente3.A5, U15.SCL
  N17: Componente3.A4, U15.SDA
  N18: U15.GPA0, KEYPAD1.7
  N19: U15.GPA1, KEYPAD1.6
  N20: U15.GPA2, KEYPAD1.5
  N21: U15.GPA3, KEYPAD1.4
  N22: U15.GPA4, KEYPAD1.3
  N23: U15.GPA5, KEYPAD1.2
  N24: U15.GPA6, KEYPAD1.1
  N25: U15.RESET, R23.Pin_1

notes:
  BATTERY POSITIVE
  TRANSFORMER POSITIVE
  SOLAR PANEL POSITIVE
  WIND CHARGER POSITIVE
  WIND CHARGER NEGATIVE
  SOLAR PANEL NEGATIVE
  TRANSFORMER NEGATIVE
  BATTERY NEGATIVE

custom parts:
  MCP23017: 16 bit I/O chip controlled via I2C
  Membrane Matrix Keypad: Membrane Matrix 3x4 Keypad

// code stored in the sketch: chargerController.fzz.ino
/*ALL THE PROGRAM IS DONE BY DARIO LOBOS, I TOOK SOME PARTS FROM EXAMPLES, 1O/MAR/2025
 * THE PROGRAM IS TO CONTROL 3 DEVICES TO CHARGE A BATTERY.
 * 
 * BOARD USED IS ARDUINO NANO 
 * 
 * DEVICE 1: IS A TRANSFORMER WITH A RECTIFIER TO HAVE DC CURRENT AND ELECTRICITY COMES FROM 
 * THE POWER SUPPLY NET. THIS CAN CHARGE AFTER A TIME SET BY THE USER. TO CHARGE BATTERY WHEN 
 * THE OTHER DEVICES DON'T REACH THE NEEDED FOR ALL NIGHT. CAN DE SET WITHOUT TIME AND BATTERY 
 * WILL BE CHARGED ALL THE DAY. BY SETTING 23:59 WILL NEVER CHARGE (OR JUST A MINUTE). I WILL 
 * ADD THE OPTION TO DISABLE BUT FOR DISABLES CAN BE DISCONNECTED,
 * 
 * 
 * DEVICE 2: IS A SOLAR PANEL THIS CHARGE WHEN BATTERY DON'T REACH THE MAXIMUN CHARGE AND WHEN
 * A PHOTO RESISTO DETERMINE THAT LIGHT IS ENOUGH TO PRODUCE CURRENT, IF NOT IS DISCONNECTED. 
 * ALSO IF VOLTAGE PRODUCED IS LEES THAN BATTERY IS DISCONNECTED, 
 * PHOTO RESISTOR VALUE CAN BE SET UP BY CONSTANT "PHOTO_PRESISTOR_LIMIT" IN THE CODE.
 * 
 * DEVICE 3: IS A WIND TURBINE AND THE ONLY RESTRICTION ARE BATTERY VOLTAGE AND DEVICE VOLTAGE.
 * 
 * I DID A MOSFET CIRCUIT FOR THIS SYSTEM AND IS HERE(Revised, added FILTERS )
 * 
 * https://drive.google.com/file/d/1AJ6Pxyg2a4SylqBItQMUnToGb4nMWeYA/view?usp=drivesdk
 *
 *
 * https://drive.google.com/file/d/1AI77g_Waz6oLzmIdAXDt1WZzXRl4m_--/view?usp=drivesdk
 * 
 * MUST BE ADJUSTED ACCORDING DEVICE CURRENT AND MOSFET USED, THERE RESISTOR CAN MORE AND LESS FIT  
 * AN IRF520.
 * 
 * CIRCUITS NEED CAPACITORS AND GROUND RESISTORS TO MAKE LESS THAN 60 HRZ LOW PASS FILTER, OTHER RESISTOR TO 
 * GROUND BIG TO DISCHARGE THE SIGNAL. 
 * 
 * FOR EXAMPLE ONE RESISTOR 12K  TO SIGNAL IN (BATTERY AND DEVICES VOLTAGE) AND 47 uf capacitor and 
 * a 5.5K (with and adjust potenciometer small) to do a voltage divider 16/5. Capacitor is to ground 
 * in parallelto R2 of voltage divider. 
 * THIS IS THE VOLTAGE DIVIDER CIRCUIT WITH A ZENER 5V AND A FUSE
 * 
 * https://drive.google.com/file/d/1ANG8-GtRzkY1PIZ6kYH60ZUBgf1YUTnj/view?usp=drivesdk
 *
 *
 * ARDUINO IS CHARGING FROM THE BATTERY  USING AN LM 7805 OR 340 WHICH IS THE SIMPLEST OPTION.
 *
 *  OPERATIONAL AMPLIFIERS NEEDS LM315 TO SET IT TO 10 VOLTS OR 12 VOLTS.
 " 
 * THE MICROCONTROLLER SEND ALL THE DATA USING FIRMATA AND WITH PHYTON IS
 " HANDLED TO MAKE HISTORIAL OF INFO AND GRAPHICS WiTH ThINKER AND PYFIRMATA.
 * Firmata is a generic protocol for communicating with microcontrolle
 * from software on a host computer. It is intended to work with
 * any host computer software package.
 *
 * To download a host software package, please clink on the following link
 * to open the download page in your default browser.
 *
 * http://firmata.org/wiki/Download
 */

/* Supports as many digital inputs and outputs as possible.
 *
 * This example code is in the public domain.

Basic program copy from examples,with analog addition and remote control switch and led pin
 done by D.Lobos March 7, 2025
 */
 //-----------------SERIAL TRANSFER PART -----------------

#include <Boards.h>
#include <Firmata.h>
#include <FirmataConstants.h>
#include <FirmataDefines.h>
#include <FirmataMarshaller.h>
#include <FirmataParser.h>

// ASSIGNMENT OF ONE PICK LOCKED FOR REMOTE CONTROL 

int PC_CONTROL_STATE= LOW;

const int PC_CONTROL_PIN= 6;

const int PC_CONTROL_MODE= OUTPUT;



byte pinPc = byte (PC_CONTROL_PIN);

byte previousPin[TOTAL_PORTS];  // PIN means PORT for input
byte previousPort[TOTAL_PORTS];
byte previousAlogPin[TOTAL_ANALOG_PINS];
byte previousAlogPort[TOTAL_ANALOG_PINS]; 
byte currentPinValue;
byte previousPinValue;


byte analogPin = 0;



void outputPort(byte port, byte value)
{
  if (IS_PIN_DIGITAL(port)){

  // only send the data when it changes, otherwise you get too many messages!
  if (previousPort[port] != value) {
    Firmata.sendDigitalPort(port, value);
    previousPort[port] = value;
delay(10);
  }
}
}
void outputAlogPort(byte port, byte value)
{
  if (IS_PIN_PWM(port)){

  // only send the data when it changes, otherwise you get too many messages!
  if (previousAlogPort[port] != value) {
    Firmata.sendAnalog(port, value);
    previousAlogPort[port] = value;
delay(10);//delay can e reduced according application.

  }
}
}




void setPinModeCallback(byte pin, int mode) {
if (PC_CONTROL_STATE ==HIGH) { 
if (pin!=pinPc) {
  if (IS_PIN_DIGITAL(pin)) {
    pinMode(PIN_TO_DIGITAL(pin), mode);
  } 
 else {pinMode(PIN_TO_PWM(pin),mode);
}
pinMode(PIN_TO_DIGITAL(pinPc), PC_CONTROL_MODE);
delay(10);
}
}
}

void digitalWriteCallback(byte port, int value)
{
if (PC_CONTROL_STATE ==HIGH) {
  byte i;
  if (IS_PIN_DIGITAL(port)){
  if (port < TOTAL_PORTS && value != previousPort[port]) {
    for (i = 0; i < 8; i++) {
      currentPinValue = (byte) value & (1 << i);
      previousPinValue = previousPort[port] & (1 << i);
      if (currentPinValue != previousPinValue) {
        digitalWrite(i + (port * 8), currentPinValue);
      }
    }
  }
  }
  
else if (port == pinPc){
for (i = 0; i < 8; i++) {
      currentPinValue = (byte) value & (1 << i);
      previousPinValue = previousPort[port] & (1 << i);
      if (currentPinValue != previousPinValue) {
        digitalWrite(i + (pinPc * 8), currentPinValue);
}
} 
}
 
previousPort[port] = value;
delay(10);
}
}

void analogWriteCallback(byte port, int value)
{
if (PC_CONTROL_STATE ==HIGH) {
byte pinPc = byte (PC_CONTROL_PIN);
  if (IS_PIN_PWM(port)) {
 if (port < TOTAL_ANALOG_PINS && value != previousAlogPort[port]) {
if (port!=pinPc) {
   
    analogWrite(PIN_TO_PWM(port), value);
}
  }
previousAlogPort[port] = value;
delay(10);
}
}
}
 
/* THIS IS FOR THE PIN EXTENDER USING THE CHIP MCP23X17 
 *  EXPANDER PIN CONNECTION:
 *  MCP         ARDUINO
 *  PIN 12 TO   A5 (I2C CLOCK)
 *  PIN 13 TO   A4 (I2C DATA)
 *  PIN 15:     GROUND (ONLY ONE EXPANDER CONNECTED, THIS IS TO ADDRESS MORE THAN ONE)
 *  PIN 16:     GROUND
 *  PIN 17:     GROUND
 *  PIN 9:      5V
 *  PIN 10:     GROUND (OF CHIP)
 *  PIN 18:     10 KOHM TO 5V  (CHIP RESET ACTIVE LOW)
 *  
 *  FROM LIBRARY README.MD
 *  When using single pin operations such as _pinMode(pinId, dir)_ or _digitalRead(pinId)_  or _digitalWrite(pinId, val)_ then the pins are addressed using the ID's below. 
 *  For example, for set the mode of _GPB0_ then use _pinMode(8, ...)_. **NOTE** The MCP23008 and MCP23S08 only have _GPAx_ pins.

| MCP23x08 Pin # | MCP23x17 Pin # | Pin Name | Pin ID |
| :------------: | :------------: | :------: | :----: |
|       10       |       21       |   GPA0   |   0    |
|       11       |       22       |   GPA1   |   1    |
|       12       |       23       |   GPA2   |   2    |
|       13       |       24       |   GPA3   |   3    |
|       14       |       25       |   GPA4   |   4    |
|       15       |       26       |   GPA5   |   5    |
|       16       |       27       |   GPA6   |   6    |
|       17       |       28       |   GPA7   |   7    |
|       --       |       1        |   GPB0   |   8    |
|       --       |       2        |   GPB1   |   9    |
|       --       |       3        |   GPB2   |   10   |
|       --       |       4        |   GPB3   |   11   |
|       --       |       5        |   GPB4   |   12   |
|       --       |       6        |   GPB5   |   13   |
|       --       |       7        |   GPB6   |   14   |
|       --       |       8        |   GPB7   |   15   |
for serial transmission is connected to pin 0 and 1 (RX,TX)
*/

#include <Adafruit_MCP23X17.h>
#include <Wire.h>;

# define MCP_PIN0 0  
# define MCP_PIN1 1  
# define MCP_PIN2 2
# define MCP_PIN3 3
# define MCP_PIN4 4
# define MCP_PIN5 5
# define MCP_PIN6 6
# define MCP_PIN7 7
# define MCP_PIN8 8
# define MCP_PIN9 9
# define MCP_PIN10 10
# define MCP_PIN11 11
# define MCP_PIN12 12
# define MCP_PIN13 13
# define MCP_PIN14 14
# define MCP_PIN15 15

 Adafruit_MCP23X17 mcp;

// DEFINE RESET PIN



// DS1302:  CE pin    -> Arduino Digital 2
//          I/O pin   -> Arduino Digital 3
//          SCLK pin  -> Arduino Digital 4

#include <DS1302.h>
DS1302 rtc(2, 3, 4);


/* LCD CONTROL PINS THIS GOES HERE IN THE ARDUINO, keyPad WILL BE IN THE EXTENDER. 
 *  keyPad WILL HAVE LESS USAGE THAN LCD ALWAYS WORKING
----------------arduino control part------------------

 * The circuit:
 * LCD RS pin to digital pin 12
 * LCD Enable pin to digital pin 11
 * LCD D4 pin to digital pin 8
 * LCD D5 pin to digital pin 7
 * LCD D6 pin to digital pin 6
 * LCD D7 pin to digital pin 5
 * LCD R/W pin to ground
 * LCD VSS pin to ground
 * LCD VCC pin to 5V
 * 10K resistor:
 * ends to +5V and ground
 * wiper to LCD VO pin (pin 3)
 Mellis
 library modified 5 Jul 2009
 by Limor Foldied (http://www.ladyada.net)
 example added 9 Jul 2009
 by Tom Igoe
 modified 22 Nov 2010
 by Tom Igoe
 modified 7 Nov 2016
 by Arturo Guadalupi

 This example code is in the public domain.

 http://www.arduino.cc/en/Tutorial/LiquidCrystalHelloWorld

 I took written parts from this example to for time reduction

*/



#include <LiquidCrystal.h>

// initialize the library by associating any needed LCD interface pin
// with the arduino pin number it is connected to
const int rs = 12, en = 11, d4 = 8, d5 = 7, d6 = 6, d7 = 5;
LiquidCrystal lcd(rs, en, d4, d5, d6, d7);

const int numRows = 2;
const int numCols = 16;

// LCD MESSAGES
const String LCD_CHARGE_MESSAGE = "BATTERY CHARGING";
const int CHARGE_LENGHT = sizeof(LCD_CHARGE_MESSAGE);
const String LCD_FULL_BATTERY = "BATTERY FULL CHARGED";
const int FULL_LENGHT = sizeof(LCD_FULL_BATTERY);
const String LCD_BATTERY_NO_CHARGE = "POWER SUPPLY DISCONECTED";
const int NO_CHARGE_LENGHT = sizeof(LCD_BATTERY_NO_CHARGE);
const String set_clock_time1 ="Set clk times?";
const String set_clock_time2 ="A=Y B=N C=Clear";
const String clock_or_time1 ="Set clk or time?";
const String clock_or_time2 ="A=Clk B=Tm *=Esc";
const String time_explain1 = "Time for start"; // devices can be two for autogeneration
const String time_explain2 = "charge from net"; // and one from public electricity company
const String time_explain3 = "public network"; // days with no sun or wind to charge.
const String time_explain4 = "for no sun& wind";
const String entry_time1 = "Insert hour 0-24";
const String entry_time2 = "Insert min. 0-60";                               
const String lcdEsc ="           *=Esc";
const String lcdMenu ="#=Menu   ";
const String ok_setup1 = "  Time stored  ";
const String ok_setup2 = "  succefully.  ";
const String ok_clear1 = "The Time stored";
const String ok_clear2 = " was erased.  ";

// BATTERY CHARACTERISTIC
// MEASSURING RANGE 3 T0 5 
// VOLTS 14 TO 12

const int PHOTO_PRESISTOR_LIMIT = 512; // VALUE MUST BE TESTED AND DETERMINE THE SOLAR PANNEL SWITCH OFF.  
int PHOTO_RESISTOR_READ=0;
const float BAT_FULL_VOLTS = 13.7;             
float batteryState = 0;
const float BAT_LOW_VOLTS = 12.5 ;

const float VOLTAGE_DIVIDER_R_TOP = 5.5 ;          // THESE ARE THE VOLTAGE DIVIDER RESISTANCE TO SEND VOLTAGE BATTERY TO
const float VOLTAGE_DIVIDER_R_GROUND = 12;          // THE ANALOG PIN DIRECTLY

const float VOLT_FACTOR = VOLTAGE_DIVIDER_R_GROUND/ (VOLTAGE_DIVIDER_R_GROUND + VOLTAGE_DIVIDER_R_TOP);
const float ANALOG_VOLTS = 5 / 1023 ;

const float CHARGER_VOLTS_1 = 16;  // THIS IS THE TRANSFORMER, SOLAR PANEL, OR OTHER DEVICE VOLTAGE. I HAVE ONLY ONE BUT LEAVE FOR 3
const float CHARGER_VOLTS_2 = 16;
const float CHARGER_VOLTS_3 = 16;


const float VOLTS_FACTOR_IN_OP = 1 ;  // THIS IS A FACTOR TO AMPLIFY THE SIGNAL FROM THE OP. AMPLIFIER 
                                      // WITH IT CAN BE MODIFIED MOSFET GATE VOLTAGE TO HAVE MORE OR LESS CURRENT .
                                      // WITHOUT CHANGE THR CIRCUIT.
                                                      
// Function to transform analog read to voltage according constant voltage divider

float analogVoltageConvertion(int read , float voltFactor)
 {
  float voltage=0;
voltage = read * ANALOG_VOLTS * voltFactor ;
return voltage;
}

// convertion from analog read to analog write

int analogConvertionToWrite(int inputread,float voltMax){
    
float inputout = float(inputread) * 255 * (voltMax-BAT_LOW_VOLTS)/1023;

if (inputout > 0){

return int(inputout);
  
}
}

// Function to display voltage and message

void lcdMessage (String message,int lenght, float analogReadVolts ){
   
   lcd.clear();
   float voltTemp=analogVoltageConvertion(analogReadVolts,VOLT_FACTOR);
   String castVolt= String(voltTemp,2);
  char castChar[sizeof(castVolt)];
   for (int i=0; i< sizeof(castVolt);i++){
   castChar[i]= castVolt.charAt(i) ; 
   }
    int thisCol=0;
    int thisRow=0;
    lcd.setCursor(thisCol, thisRow);
    lcd.print(message);
    lcd.display();
    delay(1000);
    
  // scroll positions (string length) to the left
  // to move it offscreen left:
  for (int positionCounter = 0; positionCounter < lenght ; positionCounter++) {
  // scroll one position left:
   
    lcd.scrollDisplayLeft();
    // wait a bit:
    delay(150);    
  }
  thisCol=0;
  thisRow=0;   
  lcd.clear();
  lcd.setCursor(thisCol, thisRow);
  String timeString = rtc.getTimeStr();
  String concatString = lcdMenu + timeString;
  lcd.print(concatString);
  lcd.display();
  thisCol=5;
  thisRow=1;
  lcd.setCursor(thisCol, thisRow);
   for (int i=0; i< sizeof(castVolt);i++){
    
    lcd.setCursor(thisCol+i, thisRow);
   lcd.write(castChar[i]); 
   }
}


void lcdSetupTimes (String message1, String message2){

  lcd.clear();
  int thisCol=0;
    int thisRow=0;
    lcd.setCursor(thisCol, thisRow);
    lcd.print(message1);
    lcd.display();
    thisRow=1;    
    lcd.setCursor(thisCol, thisRow);
    lcd.print(message1);
    lcd.display();
}

//
//    FILE: I2CkeyPad_keymap.ino
//  AUTHOR: Rob Tillaart
// PURPOSE: demo key mapping
//     URL: https://github.com/RobTillaart/I2CkeyPad
//
//  PCF8574 I changed the address for MCP23017 d. lobos
//    pin p0-p3 rows
//    pin p4-p7 columns
//  4x4 or smaller keyPad.


#include <Wire.h>
#include <I2CKeyPad.h>

/* KEY PAD PINS 
 *  
 *  PIN NRO.          PIN CONNECTION
 *  MCP_PIN0 0        21
 *  MCP_PIN1 1        22          
 *  MCP_PIN2 2        23
 *  MCP_PIN3 3        24
 *  MCP_PIN4 4        25
 *  MCP_PIN5 5        26
 *  MCP_PIN6 6        27
 *  MCP_PIN7 7        28
 */

const uint8_t keyPad_ADDRESS = 0x20; // address of MCP23017 chip on I2C bus PORT A. 
                                     // ARDUINO HAVE ONLY ONE IC2 PORT SO A0,A1 AND A2 IN EXTENDER GOES TO GROUND 

I2CKeyPad keyPad(keyPad_ADDRESS);

char keymap[19] = "123A456B789C*0#DNF";  // N = NoKey, F = Fail


void Setup_menu_call(){

char key = keyPad.getChar();

if (key == '#') {
          lcdTimeMainMenu(set_clock_time1,set_clock_time2);
          }

}

 //STORED TIME AND HOUR TO START CHARGE FROM PUBLIC SUPPLY NETWORK
int HOUR_FOR_CHARGE= -1;
int MINUTES_FOR_CHARGE= -1; 


void lcdTimeMainMenu (String message1, String message2) {
int timeAppend=0;
char key;

lcdSetupTimes(message1, message2);
    
while (true){
  
while (!key){
key= keyPad.getChar();
}
switch (key){
  case 'A':
  lcdmenuA();
  break;
 case 'B':
  break;
  case 'C':
  HOUR_FOR_CHARGE= -1;
  MINUTES_FOR_CHARGE= -1;
 lcdSetupTimes(ok_clear1,ok_clear2);
  break;
  case '*':
  break;
}
}
}

void lcdmenuA(){

char key;  
lcdSetupTimes(clock_or_time1, clock_or_time1);

while (true){
  
while (!key){
key = keyPad.getChar();
}
switch (key){
  case 'A':
  ClockAppend();
  break;
 case 'B':
  TimeSetAppend();
  break;
  
  case '*':
  break;
}
}  
}


void ClockAppend(){
int hours;
int minutes;  
char key;

lcdSetupTimes(entry_time1, lcdEsc);
   lcd.setCursor(10, 1);
   lcd.write(':'); 

for(int i=0;i<4;i++){

while (true){ 
key = keyPad.getChar();   
while (!key){
  key = keyPad.getChar();
}
if (key=='*'){
  break;
}
if(i==0){
  lcd.setCursor(12, 1); 
if (key>='0' && key<='2'){ 
hours = int(key)*10;
lcd.write(key);
}
}
if(i==1){
  lcd.setCursor(11, 1);

if (key>='0' && key<='9' && hours!=20 && hours!=0){
hours += int(key);
lcd.write(key);

}
if (key>='0' && key<='4' && hours==20){
hours += int(key);
lcd.write(key);
}
if (key>='1' && key<='9' && hours==0){
hours += int(key);
lcd.write(key);
}
}

if(i==2){
  lcd.setCursor(0, 0);
  lcd.print(entry_time2);
  lcd.display();
  lcd.setCursor(9, 1);

if (key>='0' && key<='6'){
minutes=int(key)*10;
lcd.write(key);
}
}

if(i==3){
  lcd.setCursor(8, 1);

if (key>='0' && key<='9'){
minutes+=int(key);
lcd.write(key);
rtc.writeProtect(false);
rtc.setTime(hours,minutes,0);
rtc.writeProtect(true);
lcdSetupTimes(ok_setup1 ,ok_setup2 );
delay(1000);

break;
}
}

}  
}
}


void TimeSetAppend(){

int hours;
int minutes;  
char key;

lcdSetupTimes(time_explain1 ,time_explain2 );
delay(1000);
lcdSetupTimes(time_explain3 ,time_explain4 );
delay(1000);

lcdSetupTimes(entry_time1, lcdEsc);
   lcd.setCursor(10, 1);
   lcd.write(':'); 

for(int i=0;i<4;i++){

while (true){ 
key = keyPad.getChar();   
while (!key){
  key = keyPad.getChar();
}
if (key=='*'){
  break;
}
if(i==0){
  lcd.setCursor(12, 1); 
if (key>='0' && key<='2'){ 
hours = int(key)*10;
lcd.write(key);
}
}
if(i==1){
  lcd.setCursor(11, 1);

if (key>='0' && key<='9' && hours!=20 && hours!=0){
hours += int(key);
lcd.write(key);

}
if (key>='0' && key<='4' && hours==20){
hours += int(key);
lcd.write(key);
}
if (key>='1' && key<='9' && hours==0){
hours += int(key);
lcd.write(key);
}
}

if(i==2){
  
  lcd.setCursor(0, 0);
  lcd.print(entry_time2);
  lcd.display();
  lcd.setCursor(9, 1);

if (key>='0' && key<='6'){
minutes=int(key)*10;
lcd.write(key);
}
}

if(i==3){
  lcd.setCursor(8, 1);

if (key>='0' && key<='9'){
minutes+=int(key);
lcd.write(key);
HOUR_FOR_CHARGE= hours;
MINUTES_FOR_CHARGE= minutes;
lcdSetupTimes(ok_setup1 ,ok_setup2 );
delay(1000);
break;
}
}

}  
}
}


// initialize constant for pins to read voltages and mosfets
// A4 and A5 ARE RESERVED FOR PIN EXTENDER BOARD, SERIAL PINS

const int MOSFET_1_PIN = A6 ;
int mosfet1Signal=0; // signal to send to the mosfet; 
const int MOSFET_2_PIN = 9 ; // digital pin can be written as analog
int mosfet2Signal=0;
const int MOSFET_3_PIN = 10 ;  // digital pin can be written as analog
int mosfet3Signal=0;

const int BATTERY_VOLTAGE_PIN= A3 ;

const int DEVICE_CHARGER_VOLTAGE_1 = A0 ;
float device1ChargerRead;
const int DEVICE_CHARGER_VOLTAGE_2 = A1 ;  
float device2ChargerRead;
const int DEVICE_CHARGER_VOLTAGE_3 = A2 ;  
float device3ChargerRead;

const int PHOTO_RESISTOR = A7 ; 


void setup()
{  

// initialize the PC control pin as an output:
  pinMode(PC_CONTROL_PIN, PC_CONTROL_MODE);

// initialize firmata  
  Firmata.setFirmwareVersion(FIRMATA_MAJOR_VERSION, FIRMATA_MINOR_VERSION);
  Firmata.attach(DIGITAL_MESSAGE, digitalWriteCallback);
Firmata.attach(ANALOG_MESSAGE, analogWriteCallback);
  Firmata.attach(SET_PIN_MODE, setPinModeCallback);
  Firmata.begin(57600);

 // Set the clock to run-mode, and disable the write protection
  rtc.halt(false);
  rtc.writeProtect(true);
  
// SerialBegin for MCP extension board chip 
 Serial.begin(115200);

while( !Serial ){/*wait*/}   //for USB serial switching boards
  Wire.begin( );
  Wire.setClock(400000);
   if (keyPad.begin() == false)
  {
    Serial.println("\nERROR: cannot communicate to keyPad.\nPlease reboot.\n");
    while (1);
  }             
  keyPad.loadKeyMap(keymap);
 
// LCD display 16 x 2 configuration 
  lcd.begin(numCols, numRows);
  
// BEGIN AND PIN ASSIGMENT IN MCP23017 

mcp.begin_I2C();
mcp.pinMode(3, OUTPUT);


// pin assigment modes
  pinMode( MOSFET_1_PIN, OUTPUT);
  pinMode( MOSFET_2_PIN, OUTPUT);
  pinMode( MOSFET_3_PIN, OUTPUT);
  pinMode( DEVICE_CHARGER_VOLTAGE_1, INPUT);
  pinMode( DEVICE_CHARGER_VOLTAGE_2, INPUT);
  pinMode( DEVICE_CHARGER_VOLTAGE_3, INPUT);
  pinMode( PHOTO_RESISTOR, INPUT);
  pinMode( BATTERY_VOLTAGE_PIN, INPUT);

// keyPadaddEventListener(keyPadEvemt); // Listener to detect pressed key l.istener don't work in extender MCP


}

void loop(){
  
  while (PC_CONTROL_STATE == LOW) {
    
  while (Firmata.available()) {
    Firmata.processInput();
if (PC_CONTROL_STATE == HIGH){
break;
}
//-----------------------------------
//Arduino program control
//-----------------------------------

Setup_menu_call();

batteryState = analogVoltageConvertion(analogRead(BATTERY_VOLTAGE_PIN),VOLT_FACTOR);
device1ChargerRead= analogVoltageConvertion(analogRead(DEVICE_CHARGER_VOLTAGE_1),VOLTS_FACTOR_IN_OP);
device2ChargerRead= analogVoltageConvertion(analogRead(DEVICE_CHARGER_VOLTAGE_2),VOLTS_FACTOR_IN_OP);
device3ChargerRead= analogVoltageConvertion (analogRead(DEVICE_CHARGER_VOLTAGE_3),VOLTS_FACTOR_IN_OP);
PHOTO_RESISTOR_READ = analogRead(PHOTO_RESISTOR);
  
while (batteryState <  BAT_FULL_VOLTS) {




mosfet1Signal = analogConvertionToWrite(device1ChargerRead,CHARGER_VOLTS_1); // I ONLY HAVE ONE DEVICE UP TO NOW
mosfet2Signal = analogConvertionToWrite(device2ChargerRead,CHARGER_VOLTS_2);
mosfet3Signal = analogConvertionToWrite(device3ChargerRead,CHARGER_VOLTS_3);

if (mosfet1Signal ==0 &&  mosfet2Signal ==0 && mosfet3Signal ==0){
lcdMessage (LCD_BATTERY_NO_CHARGE,NO_CHARGE_LENGHT, batteryState );
}
else{
  lcdMessage (LCD_CHARGE_MESSAGE,CHARGE_LENGHT, batteryState );

}


String timeclk = rtc.getTimeStr(FORMAT_SHORT);
char hourclk[]= {timeclk.charAt(0),timeclk.charAt(1),timeclk.charAt(3), timeclk.charAt(4)};
int timeint=-1;
for (int i=0;i<4;i++){
timeint += hourclk[i]*10^(3-i);
}
if(timeint>=0){
  timeint+=1;
}

int storedTime= HOUR_FOR_CHARGE^100+ MINUTES_FOR_CHARGE;

if (storedTime <= timeint){
analogWrite(MOSFET_1_PIN,mosfet1Signal); // SIGNAL TO TRANSFORMER MOSFET
}

if ( PHOTO_RESISTOR_READ > PHOTO_PRESISTOR_LIMIT){
analogWrite(MOSFET_2_PIN,mosfet2Signal); // SIGNAL TO SOLAR PANNEL
}

analogWrite(MOSFET_3_PIN,mosfet3Signal); // SIGNAL FOR WIND GENERATOR


   
// Last sentences to update communication with PC

  byte i;


  for (i = 0; i < TOTAL_PORTS; i++) {
    outputPort(i, readPort(i,0xff));
    
  }
for (i = 0; i < TOTAL_ANALOG_PINS; i++) {
outputAlogPort(i, analogRead(i));
    
  }

  while (Firmata.available()) {
    Firmata.processInput();
 PC_CONTROL_STATE = digitalRead(PC_CONTROL_PIN);
  }
}
lcdMessage (LCD_FULL_BATTERY,FULL_LENGHT, batteryState );
}

  }
  
while (PC_CONTROL_STATE== HIGH) {
//
// pc program that will be only call back process and read check.

while (Firmata.available()) {
    Firmata.processInput();
}
  byte i;


  for (i = 0; i < TOTAL_PORTS; i++) {
    outputPort(i, readPort(i,0xff));
    
  }
for (i = 0; i < TOTAL_ANALOG_PINS; i++) {
outputAlogPort(i, analogRead(i));
    
  }

  while (Firmata.available()) {
    Firmata.processInput();

}
PC_CONTROL_STATE = digitalRead(PC_CONTROL_PIN);
}
// reset is necessary because the computer
// can change pins or ports and modes of operation  so is necessary hardware with a jumper and reset pin.
// create a standard reset function
// THE RESET PIN MUST BE CONNECTED TO THE MCP23X17 PHYSICAL PIN NR. 8 (pin ID 15) 

mcp.digitalWrite(MCP_PIN15, HIGH);


  }  





// END OF FILE
